# Fritzing sketch integrated (saved by Fritzing 0.9.4)
circuit board: 10.0961cm x 8.17199cm
breadboards: 2

parts:
  R5 = Resistor [tolerance=±5% resistance=150 package=THT]
  R6 = Resistor [tolerance=±5% resistance=150 package=THT]
  IC3 = MCP2515 [package=THT]
  C6 = Ceramic Capacitor [capacitance=27pF package="100 mil [THT, multilayer]"]
  C7 = Ceramic Capacitor [capacitance=27pF package="100 mil [THT, multilayer]"]
  XTAL2 = Crystal [frequency="16 Mhz" package=THT]
  LED4 = LED - 3mm [color="Blue (430nm)" package="3 mm [THT]"]
  LED5 = LED - 3mm [color="Blue (430nm)" package="3 mm [THT]"]
  R7 = Resistor [tolerance=±5% resistance=47k package=THT]
  IC4 = IC, DIP package, 8 pins [chip_label=2551 part_number=MCP2551]
  XTAL3 = Crystal [frequency="16 Mhz" package=THT]
  U2 = atmega328 [package=dip]
  IC6 = Voltage Regulator [package=78xxl]
  C9 = Electrolytic Capacitor [capacitance=10μF package="0605 [SMD, electrolytic]"]
  C10 = Electrolytic Capacitor [capacitance=10μF part_number=xxx package="0605 [SMD, electrolytic]"]
  C11 = Ceramic Capacitor [capacitance=27pF package="100 mil [THT, multilayer]"]
  C12 = Ceramic Capacitor [capacitance=27pF package="100 mil [THT, multilayer]"]
  J5 = Camdenboss CTB0158-2 [part_number=CTB0158-2 package=THT]
  J4 = Camdenboss CTB0158-2 [part_number=CTB0158-2 package=THT]
  R8 = Resistor [tolerance=±5% resistance=10k package=THT]
  Part1 = Analog Digital MUX Breakout  # not connected

nets:
  VDD: R5.Pin_0, R6.Pin_0, IC3.Vdd, IC4.pin3, U2.VCC, U2.AVCC, IC6.OUT, C10.+, R8.Pin_0
  N1: R5.Pin_1, LED4.cathode
  N2: R6.Pin_1, IC3.RXCAN, LED5.cathode, LED5.anode, IC4.pin4
  N3: IC3.TXCAN, LED4.anode, IC4.pin1
  N4: IC3.OSC2, C6.1, XTAL2.pin_0
  N5: IC3.OSC1, C7.1, XTAL2.pin_1
  GND: IC3.Vss, C6.0, C7.0, R7.Pin_1, U2.GND, IC6.GND, C9.-, C10.-, C11.0, C12.0, J5.pin2
  N6: IC3.INT, U2.D9_(PWM)
  N7: IC3.SCK, U2.D13
  N8: IC3.SI, U2.D11_(PWM)
  N9: IC3.SO, U2.D12
  N10: IC3.CS, U2.D10_(PWM)
  N11: R7.Pin_0, IC4.pin8
  N12: IC4.pin6, IC4.pin7, J4.pin1, J4.pin2
  N13: XTAL3.pin_0, U2.XLAT2, C12.1
  N14: XTAL3.pin_1, U2.XLAT1, C11.1
  N15: U2.RESET, R8.Pin_1
  N16: IC6.IN, C9.+, J5.pin1

custom parts:
  MCP2515: MCP2515 CAN Controller with SPI Interface
