# Fritzing sketch prototype (saved by Fritzing 0.9.4)
circuit board: 8.46667cm x 5.64444cm
breadboards: 1

parts:
  M1 = Niren can bus module [package=THT]
  J1 = Power Jack [package=power_jack_pth_lock]
  C2 = Capacitor Polarized [part_number=10uF package=cpol-radial-10uf-25v]
  LED1 = smd LED [color="Red (633nm)" package="1206 [SMD]"]
  IC1 = Voltage Regulator [package=78xxl]
  C3 = Capacitor Polarized [part_number=100uF package=panasonic_d]
  R1 = Resistor [tolerance=±5% resistance=220 package="2512 [SMD]"]
  Part1 = Arduino Uno (Rev3)
  U1 = OBDII [package=obdii]

nets:
  N1: M1.pin1, M1.pin2, C2.-, LED1.cathode, LED1.anode, IC1.OUT, R1.Pin_0, R1.Pin_1, Part1.GND
  N2: M1.pin3, Part1.D10_PWM/SS
  N3: M1.pin4, Part1.D12/MISO
  N4: M1.pin5, M1.pin6, M1.pin7, Part1.D11_PWM/MOSI, Part1.D13/SCK, Part1.D2
  N5: M1.pin10, U1.J1850BUS, U1.11, U1.12, U1.13, U1.CANLOW
  N6: M1.pin11, U1.3
  GND: J1.GND, J1.GNDBREAK, C2.+, IC1.GND, C3.+
  N7: J1.PWR, IC1.IN, C3.-

custom parts:
  Niren can bus module: Niren can bus module availabe on ebay and others. No pcb view as no mechanical drawng and it wouldn't mount anyway.
