# Fritzing sketch prototypeRECOVER2 (saved by Fritzing 0.9.4)
circuit board: 8.46667cm x 5.64444cm
breadboards: 1

parts:
  IC2 = MCP2515 [package=THT]
  IC3 = IC, DIP package, 8 pins [chip_label=2551 part_number=MCP2551]
  R2 = Resistor [tolerance=±5% resistance=150 package=THT]
  C4 = Ceramic Capacitor [capacitance=27pF package="100 mil [THT, multilayer]"]
  C5 = Ceramic Capacitor [capacitance=27pF package="100 mil [THT, multilayer]"]
  XTAL1 = Crystal [frequency="16 Mhz" package=THT]
  R3 = Resistor [tolerance=±5% resistance=150 package=THT]
  R4 = Resistor [tolerance=±5% resistance=47k package=THT]
  LED2 = LED - 3mm [color="Blue (430nm)" package="3 mm [THT]"]
  LED3 = LED - 3mm [color="Blue (430nm)" package="3 mm [THT]"]
  J3 = Camdenboss CTB0158-4 [part_number=CTB0158-4 package=THT]
  U1 = atmega328 [package=dip]
  XTAL2 = Crystal [frequency="16 Mhz" package=THT]
  IC5 = Voltage Regulator [package=78xxl]  # not connected
  C7 = Electrolytic Capacitor [capacitance=10μF package="0605 [SMD, electrolytic]"]  # not connected
  C8 = Electrolytic Capacitor [capacitance=10μF package="0605 [SMD, electrolytic]"]  # not connected

nets:
  N1: IC2.TXCAN, IC3.pin1, LED2.anode
  N2: IC2.RXCAN, IC3.pin4, LED3.cathode
  N3: IC2.OSC2, C4.0, XTAL1.pin_1
  N4: IC2.OSC1, C5.1, XTAL1.pin_0
  N5: IC2.Vss, IC3.pin2, C4.1, C5.0, R4.Pin_1, J3.pin4
  N6: IC2.Vdd, IC3.pin3, R2.Pin_0, R3.Pin_0, J3.pin3
  N7: IC3.pin6, J3.pin1
  N8: IC3.pin7, J3.pin2
  N9: IC3.pin8, R4.Pin_0
  N10: R2.Pin_1, LED2.cathode
  N11: R3.Pin_1, LED3.anode
  N12: U1.XLAT1, XTAL2.pin_1
  N13: U1.XLAT2, XTAL2.pin_0

custom parts:
  MCP2515: MCP2515 CAN Controller with SPI Interface
